// Logisim project relogio1.circ as structural Verilog: 3 circuits, main circuit main
// Minutos
module main (
  input  POWER,
  input  Start___Pause,
  input  in_3
);

  wire flip_flop_1_out_8, flip_flop_1_out_9, flip_flop_1_out_10, flip_flop_1_out_11, flip_flop_1_out_12,
       flip_flop_1_out_13, flip_flop_1_out_14, flip_flop_1_out_15, flip_flop_1_out_16, flip_flop_1_out_17,
       flip_flop_1_out_18, flip_flop_1_out_19, flip_flop_1_out_20, flip_flop_1_out_21, flip_flop_1_out_22,
       flip_flop_1_out_23, flip_flop_1_out_24, flip_flop_1_out_25, flip_flop_1_out_26, flip_flop_1_out_27,
       flip_flop_1_out_28, flip_flop_1_out_29, flip_flop_1_out_30, flip_flop_1_out_31, flip_flop_1_out_32,
       flip_flop_1_out_33, flip_flop_1_out_34, flip_flop_1_out_35, flip_flop_1_out_36, flip_flop_1_out_37,
       flip_flop_1_out_38, flip_flop_1_out_39, flip_flop_1_out_40, flip_flop_1_out_41, flip_flop_1_out_42,
       flip_flop_1_out_43, flip_flop_1_out_44, flip_flop_1_out_45, flip_flop_1_out_46, flip_flop_1_out_47,
       flip_flop_1_out_48, flip_flop_1_out_49, flip_flop_1_out_50, flip_flop_1_out_51, Horas_out,
       Minutos_out, not_1_out, RESET_out, Segundos_out;

  Button RESET (.out(RESET_out));
  _7_Segment_Display u_7_segment_display_1 (
    .g(flip_flop_1_out_42), .f(flip_flop_1_out_41), .a(flip_flop_1_out_36), .b(flip_flop_1_out_37),
    .e(flip_flop_1_out_40), .d(flip_flop_1_out_39), .c(flip_flop_1_out_38));  // open: dp
  _7_Segment_Display u_7_segment_display_2 (
    .g(flip_flop_1_out_49), .f(flip_flop_1_out_48), .a(flip_flop_1_out_43), .b(flip_flop_1_out_44),
    .e(flip_flop_1_out_47), .d(flip_flop_1_out_46), .c(flip_flop_1_out_45));  // open: dp
  _7_Segment_Display u_7_segment_display_3 (
    .g(flip_flop_1_out_35), .f(flip_flop_1_out_34), .a(flip_flop_1_out_29), .b(flip_flop_1_out_30),
    .e(flip_flop_1_out_33), .d(flip_flop_1_out_32), .c(flip_flop_1_out_31));  // open: dp
  Button Horas (.out(Horas_out));
  Flip_flop flip_flop_1 (
    .in_2(POWER), .out_8(flip_flop_1_out_8), .out_9(flip_flop_1_out_9), .out_10(flip_flop_1_out_10),
    .out_11(flip_flop_1_out_11), .out_12(flip_flop_1_out_12), .out_13(flip_flop_1_out_13),
    .out_14(flip_flop_1_out_14), .out_15(flip_flop_1_out_15), .out_16(flip_flop_1_out_16),
    .out_17(flip_flop_1_out_17), .out_18(flip_flop_1_out_18), .out_19(flip_flop_1_out_19),
    .out_20(flip_flop_1_out_20), .out_21(flip_flop_1_out_21), .out_22(flip_flop_1_out_22),
    .out_23(flip_flop_1_out_23), .out_24(flip_flop_1_out_24), .out_25(flip_flop_1_out_25),
    .out_26(flip_flop_1_out_26), .out_27(flip_flop_1_out_27), .out_28(flip_flop_1_out_28),
    .out_29(flip_flop_1_out_29), .out_30(flip_flop_1_out_30), .out_31(flip_flop_1_out_31),
    .out_32(flip_flop_1_out_32), .out_33(flip_flop_1_out_33), .out_34(flip_flop_1_out_34),
    .out_35(flip_flop_1_out_35), .out_36(flip_flop_1_out_36), .out_37(flip_flop_1_out_37),
    .out_38(flip_flop_1_out_38), .out_39(flip_flop_1_out_39), .out_40(flip_flop_1_out_40),
    .out_41(flip_flop_1_out_41), .out_42(flip_flop_1_out_42), .out_43(flip_flop_1_out_43),
    .out_44(flip_flop_1_out_44), .out_45(flip_flop_1_out_45), .out_46(flip_flop_1_out_46),
    .out_47(flip_flop_1_out_47), .out_48(flip_flop_1_out_48), .out_49(flip_flop_1_out_49),
    .in_1(Start___Pause), .in_5(Minutos_out), .in_6(Horas_out), .in_3(Segundos_out), .in_7(in_3),
    .in_4(RESET_out), .out_50(flip_flop_1_out_50), .out_51(flip_flop_1_out_51));
  _7_Segment_Display u_7_segment_display_4 (
    .g(flip_flop_1_out_28), .f(flip_flop_1_out_27), .a(flip_flop_1_out_22), .b(flip_flop_1_out_23),
    .e(flip_flop_1_out_26), .d(flip_flop_1_out_25), .c(flip_flop_1_out_24));  // open: dp
  Button Minutos (.out(Minutos_out));
  _7_Segment_Display u_7_segment_display_5 (
    .g(flip_flop_1_out_21), .f(flip_flop_1_out_20), .a(flip_flop_1_out_15), .b(flip_flop_1_out_16),
    .e(flip_flop_1_out_19), .d(flip_flop_1_out_18), .c(flip_flop_1_out_17));  // open: dp
  Button Segundos (.out(Segundos_out));
  _7_Segment_Display u_7_segment_display_6 (
    .g(flip_flop_1_out_14), .f(flip_flop_1_out_13), .a(flip_flop_1_out_8), .b(flip_flop_1_out_9),
    .e(flip_flop_1_out_12), .d(flip_flop_1_out_11), .c(flip_flop_1_out_10));  // open: dp
  not not_1 (not_1_out, in_3);
  LED _24hrs (.in(not_1_out));
  LED _12hrs (.in(in_3));
  LED AM (.in(flip_flop_1_out_51));
  LED PM (.in(flip_flop_1_out_50));

  // Notes on the sheet:
  //   HORAS
  //   MINUTOS
  //   SEGUNDOS
endmodule

module CONTADOR (
  input  x,
  input  y,
  input  w,
  input  z,
  output A,
  output B,
  output C,
  output D,
  output E,
  output F,
  output G
);

  wire and_1_out, and_2_out, and_3_out, and_4_out, and_5_out, and_6_out, and_7_out, and_8_out, and_9_out,
       and_10_out, and_11_out, and_12_out, and_13_out, and_14_out, and_15_out, and_16_out, not_1_out,
       not_2_out, not_3_out, not_4_out, not_5_out, not_6_out, not_7_out, not_8_out, not_9_out, not_10_out,
       not_11_out, not_12_out, not_13_out, not_14_out, not_15_out, not_16_out, not_17_out, not_18_out,
       not_19_out, not_20_out, not_21_out;

  not not_1 (not_1_out, y);
  and and_1 (and_1_out, not_1_out, not_2_out);
  not not_2 (not_2_out, z);
  and and_2 (and_2_out, y, z);
  not not_3 (not_3_out, y);
  not not_4 (not_4_out, w);
  and and_3 (and_3_out, not_4_out, not_5_out);
  not not_5 (not_5_out, z);
  and and_4 (and_4_out, w, z);
  not not_6 (not_6_out, w);
  or or_1 (C, not_6_out, z, y);
  not not_7 (not_7_out, y);
  and and_5 (and_5_out, not_7_out, not_8_out);
  not not_8 (not_8_out, z);
  not not_9 (not_9_out, y);
  and and_6 (and_6_out, not_9_out, w);
  and and_7 (and_7_out, w, not_10_out);
  not not_10 (not_10_out, z);
  not not_11 (not_11_out, w);
  and and_8 (and_8_out, y, not_11_out, z);
  not not_12 (not_12_out, y);
  and and_9 (and_9_out, not_12_out, not_13_out);
  not not_13 (not_13_out, z);
  and and_10 (and_10_out, w, not_14_out);
  not not_14 (not_14_out, z);
  not not_15 (not_15_out, w);
  and and_11 (and_11_out, not_15_out, not_16_out);
  not not_16 (not_16_out, z);
  and and_12 (and_12_out, y, not_17_out);
  not not_17 (not_17_out, w);
  and and_13 (and_13_out, y, not_18_out);
  not not_18 (not_18_out, z);
  not not_19 (not_19_out, y);
  and and_14 (and_14_out, not_19_out, w);
  and and_15 (and_15_out, y, not_20_out);
  not not_20 (not_20_out, w);
  and and_16 (and_16_out, y, not_21_out);
  not not_21 (not_21_out, z);
  or or_2 (A, and_1_out, w, and_2_out, x);
  or or_3 (B, not_3_out, and_3_out, and_4_out);
  or or_4 (D, and_5_out, and_6_out, and_7_out, and_8_out, x);
  or or_5 (E, and_9_out, and_10_out);
  or or_6 (F, and_11_out, and_12_out, and_13_out, x);
  or or_7 (G, and_14_out, and_15_out, and_16_out, x);
endmodule

module Flip_flop (
  input  in_1,
  input  in_2,
  input  in_3,
  input  in_4,
  input  in_5,
  input  in_6,
  input  in_7,
  output out_8,
  output out_9,
  output out_10,
  output out_11,
  output out_12,
  output out_13,
  output out_14,
  output out_15,
  output out_16,
  output out_17,
  output out_18,
  output out_19,
  output out_20,
  output out_21,
  output out_22,
  output out_23,
  output out_24,
  output out_25,
  output out_26,
  output out_27,
  output out_28,
  output out_29,
  output out_30,
  output out_31,
  output out_32,
  output out_33,
  output out_34,
  output out_35,
  output out_36,
  output out_37,
  output out_38,
  output out_39,
  output out_40,
  output out_41,
  output out_42,
  output out_43,
  output out_44,
  output out_45,
  output out_46,
  output out_47,
  output out_48,
  output out_49,
  output out_50,
  output out_51
);

  wire and_1_out, and_2_out, and_3_out, and_4_out, and_5_out, and_6_out, and_7_out, and_8_out, and_9_out,
       clock_1_out, j_k_ff_1_q, j_k_ff_1_qn, j_k_ff_2_q, j_k_ff_2_qn, j_k_ff_3_q, j_k_ff_3_qn, j_k_ff_4_q,
       j_k_ff_4_qn, j_k_ff_5_q, j_k_ff_5_qn, j_k_ff_6_q, j_k_ff_6_qn, j_k_ff_7_q, j_k_ff_7_qn, j_k_ff_8_q,
       j_k_ff_8_qn, j_k_ff_9_q, j_k_ff_9_qn, j_k_ff_10_q, j_k_ff_10_qn, j_k_ff_11_q, j_k_ff_11_qn,
       j_k_ff_12_q, j_k_ff_12_qn, j_k_ff_14_q, j_k_ff_14_qn, j_k_ff_15_q, j_k_ff_15_qn, j_k_ff_16_q,
       j_k_ff_16_qn, j_k_ff_17_q, j_k_ff_17_qn, j_k_ff_18_q, j_k_ff_19_q, j_k_ff_19_qn, j_k_ff_20_q,
       j_k_ff_20_qn, j_k_ff_21_q, j_k_ff_22_q, j_k_ff_23_q, j_k_ff_24_q, j_k_ff_25_q, not_1_out, not_2_out,
       not_3_out, not_4_out, not_5_out, not_6_out, not_7_out, not_8_out, or_1_out, or_2_out, or_3_out,
       or_4_out, or_5_out, or_6_out, or_7_out, or_8_out, or_9_out, or_10_out, or_11_out, or_12_out;

  and and_1 (and_1_out, in_1, clock_1_out);
  and and_2 (and_2_out, in_7, j_k_ff_11_q, j_k_ff_5_q, j_k_ff_6_q);
  Clock clock_1 (.out(clock_1_out));
  or or_1 (or_1_out, and_2_out, j_k_ff_5_q);
  or or_2 (or_2_out, in_3, and_1_out);
  or or_3 (or_3_out, not_1_out, in_4, and_4_out);
  not not_1 (not_1_out, in_2);
  or or_4 (or_4_out, not_2_out, in_4, and_5_out);
  not not_2 (not_2_out, in_2);
  or or_5 (or_5_out, and_5_out, in_5);
  or or_6 (or_6_out, not_3_out, in_4, and_6_out);
  not not_3 (not_3_out, in_2);
  or or_7 (or_7_out, not_4_out, in_4, and_7_out);
  not not_4 (not_4_out, in_2);
  and and_3 (and_3_out, j_k_ff_12_q, j_k_ff_19_q);
  J_K_Flip_Flop j_k_ff_1 (
    .J(in_2), .clk(or_2_out), .K(in_2), .Q(j_k_ff_1_q), .Qn(j_k_ff_1_qn), .reset(or_3_out));  // open: preset, en
  or or_8 (or_8_out, and_7_out, in_6);
  or or_9 (or_9_out, in_4, and_3_out, not_5_out, and_8_out);
  not not_5 (not_5_out, in_2);
  and and_4 (and_4_out, j_k_ff_7_q, j_k_ff_18_q);
  J_K_Flip_Flop j_k_ff_2 (
    .J(in_2), .clk(and_4_out), .K(in_2), .Q(j_k_ff_2_q), .Qn(j_k_ff_2_qn), .reset(or_4_out));  // open: preset, en
  and and_5 (and_5_out, j_k_ff_8_q, j_k_ff_15_q);
  J_K_Flip_Flop j_k_ff_3 (
    .J(in_2), .clk(or_5_out), .K(in_2), .Q(j_k_ff_3_q), .Qn(j_k_ff_3_qn), .reset(or_6_out));  // open: preset, en
  and and_6 (and_6_out, j_k_ff_9_q, j_k_ff_22_q);
  J_K_Flip_Flop j_k_ff_4 (
    .J(in_2), .clk(and_6_out), .K(in_2), .Q(j_k_ff_4_q), .Qn(j_k_ff_4_qn), .reset(or_7_out));  // open: preset, en
  and and_7 (and_7_out, j_k_ff_10_q, j_k_ff_17_q);
  J_K_Flip_Flop j_k_ff_5 (
    .J(in_2), .clk(or_8_out), .K(in_2), .Q(j_k_ff_5_q), .Qn(j_k_ff_5_qn), .reset(or_9_out));  // open: preset, en
  J_K_Flip_Flop j_k_ff_6 (
    .J(in_2), .clk(or_9_out), .K(in_2), .Q(j_k_ff_6_q), .Qn(j_k_ff_6_qn), .reset(or_10_out));  // open: preset, en
  or or_10 (or_10_out, in_4, not_6_out, and_9_out, and_2_out);
  not not_6 (not_6_out, in_2);
  or or_11 (or_11_out, not_8_out, in_4, not_7_out);
  not not_7 (not_7_out, in_2);
  not not_8 (not_8_out, in_7);
  J_K_Flip_Flop j_k_ff_7 (
    .J(in_2), .clk(j_k_ff_1_qn), .K(in_2), .Q(j_k_ff_7_q), .Qn(j_k_ff_7_qn), .reset(or_3_out));  // open: preset, en
  J_K_Flip_Flop j_k_ff_8 (
    .J(in_2), .clk(j_k_ff_2_qn), .K(in_2), .Q(j_k_ff_8_q), .Qn(j_k_ff_8_qn), .reset(or_4_out));  // open: preset, en
  J_K_Flip_Flop j_k_ff_9 (
    .J(in_2), .clk(j_k_ff_3_qn), .K(in_2), .Q(j_k_ff_9_q), .Qn(j_k_ff_9_qn), .reset(or_6_out));  // open: preset, en
  J_K_Flip_Flop j_k_ff_10 (
    .J(in_2), .clk(j_k_ff_4_qn), .K(in_2), .Q(j_k_ff_10_q), .Qn(j_k_ff_10_qn), .reset(or_7_out));  // open: preset, en
  J_K_Flip_Flop j_k_ff_11 (
    .J(in_2), .clk(j_k_ff_5_qn), .K(in_2), .Q(j_k_ff_11_q), .Qn(j_k_ff_11_qn), .reset(or_12_out));  // open: preset, en
  or or_12 (or_12_out, or_9_out, and_2_out);
  and and_8 (and_8_out, j_k_ff_11_q, j_k_ff_24_q);
  J_K_Flip_Flop j_k_ff_12 (
    .J(in_2), .clk(j_k_ff_6_qn), .K(in_2), .Q(j_k_ff_12_q), .Qn(j_k_ff_12_qn), .reset(or_10_out));  // open: preset, en
  and and_9 (and_9_out, j_k_ff_12_q, j_k_ff_6_q);
  J_K_Flip_Flop j_k_ff_13 (
    .J(in_7), .clk(and_2_out), .K(in_7), .Q(out_50), .Qn(out_51), .reset(or_11_out));  // open: preset, en
  J_K_Flip_Flop j_k_ff_14 (
    .J(in_2), .clk(j_k_ff_7_qn), .K(in_2), .Q(j_k_ff_14_q), .Qn(j_k_ff_14_qn), .reset(or_3_out));  // open: preset, en
  J_K_Flip_Flop j_k_ff_15 (
    .J(in_2), .clk(j_k_ff_8_qn), .K(in_2), .Q(j_k_ff_15_q), .Qn(j_k_ff_15_qn), .reset(or_4_out));  // open: preset, en
  J_K_Flip_Flop j_k_ff_16 (
    .J(in_2), .clk(j_k_ff_9_qn), .K(in_2), .Q(j_k_ff_16_q), .Qn(j_k_ff_16_qn), .reset(or_6_out));  // open: preset, en
  J_K_Flip_Flop j_k_ff_17 (
    .J(in_2), .clk(j_k_ff_10_qn), .K(in_2), .Q(j_k_ff_17_q), .Qn(j_k_ff_17_qn), .reset(or_7_out));  // open: preset, en
  J_K_Flip_Flop j_k_ff_18 (
    .J(in_2), .clk(j_k_ff_14_qn), .K(in_2), .Q(j_k_ff_18_q), .reset(or_3_out));  // open: Qn, preset, en
  J_K_Flip_Flop j_k_ff_19 (
    .J(in_2), .clk(j_k_ff_11_qn), .K(in_2), .Q(j_k_ff_19_q), .Qn(j_k_ff_19_qn), .reset(or_12_out));  // open: preset, en
  J_K_Flip_Flop j_k_ff_20 (
    .J(in_2), .clk(j_k_ff_12_qn), .K(in_2), .Q(j_k_ff_20_q), .Qn(j_k_ff_20_qn), .reset(or_10_out));  // open: preset, en
  J_K_Flip_Flop j_k_ff_21 (
    .J(in_2), .clk(j_k_ff_15_qn), .K(in_2), .Q(j_k_ff_21_q), .reset(or_4_out));  // open: Qn, preset, en
  J_K_Flip_Flop j_k_ff_22 (
    .J(in_2), .clk(j_k_ff_16_qn), .K(in_2), .Q(j_k_ff_22_q), .reset(or_6_out));  // open: Qn, preset, en
  J_K_Flip_Flop j_k_ff_23 (
    .J(in_2), .clk(j_k_ff_17_qn), .K(in_2), .Q(j_k_ff_23_q), .reset(or_7_out));  // open: Qn, preset, en
  J_K_Flip_Flop j_k_ff_24 (
    .J(in_2), .clk(j_k_ff_19_qn), .K(in_2), .Q(j_k_ff_24_q), .reset(or_12_out));  // open: Qn, preset, en
  J_K_Flip_Flop j_k_ff_25 (
    .J(in_2), .clk(j_k_ff_20_qn), .K(in_2), .Q(j_k_ff_25_q), .reset(or_10_out));  // open: Qn, preset, en
  CONTADOR contador_1 (
    .x(j_k_ff_18_q), .y(j_k_ff_14_q), .w(j_k_ff_7_q), .z(j_k_ff_1_q), .A(out_8), .B(out_9), .C(out_10),
    .D(out_11), .E(out_12), .F(out_13), .G(out_14));
  CONTADOR contador_2 (
    .x(j_k_ff_21_q), .y(j_k_ff_15_q), .w(j_k_ff_8_q), .z(j_k_ff_2_q), .A(out_15), .B(out_16), .C(out_17),
    .D(out_18), .E(out_19), .F(out_20), .G(out_21));
  CONTADOR contador_3 (
    .x(j_k_ff_22_q), .y(j_k_ff_16_q), .w(j_k_ff_9_q), .z(j_k_ff_3_q), .A(out_22), .B(out_23), .C(out_24),
    .D(out_25), .E(out_26), .F(out_27), .G(out_28));
  CONTADOR contador_4 (
    .x(j_k_ff_23_q), .y(j_k_ff_17_q), .w(j_k_ff_10_q), .z(j_k_ff_4_q), .A(out_29), .B(out_30), .C(out_31),
    .D(out_32), .E(out_33), .F(out_34), .G(out_35));
  CONTADOR contador_5 (
    .x(j_k_ff_24_q), .y(j_k_ff_19_q), .w(j_k_ff_11_q), .z(or_1_out), .A(out_36), .B(out_37), .C(out_38),
    .D(out_39), .E(out_40), .F(out_41), .G(out_42));
  CONTADOR contador_6 (
    .x(j_k_ff_25_q), .y(j_k_ff_20_q), .w(j_k_ff_12_q), .z(j_k_ff_6_q), .A(out_43), .B(out_44), .C(out_45),
    .D(out_46), .E(out_47), .F(out_48), .G(out_49));
endmodule
